// Logisim project microProcessor_frog.circ as structural Verilog: 4 circuits, main circuit main
module main (
);

  wire [11:0] register_1_q;
  wire [15:0] alu_1_result, multiplexer_1_out, multiplexer_2_out, multiplexer_3_out, pc_1_pc, ram_1_data,
       regbank_1_out_5, regbank_1_out_6, regbank_1_out_7, regbank_1_out_8;

  PC pc_1 (.pc(pc_1_pc));  // open: PC_INC
  RAM #(.addrWidth(16), .dataWidth(16), .bus("separate")) ram_1 (
    .addr(pc_1_pc), .data(ram_1_data));  // open: din, str, sel, clk, ld, clr
  regbank regbank_1 (
    .REGSEL(register_1_q[1:0]), .Din(multiplexer_1_out), .out_5(regbank_1_out_5), .out_6(regbank_1_out_6),
    .out_7(regbank_1_out_7), .out_8(regbank_1_out_8));  // open: LD, clock
  Multiplexer #(.width(16), .enable("false")) multiplexer_1 (
    .in0(alu_1_result), .in1(ram_1_data), .out(multiplexer_1_out));  // open: sel
  Multiplexer #(.select(2), .width(16), .enable("false")) multiplexer_2 (
    .in0(regbank_1_out_5), .in1(regbank_1_out_6), .in2(regbank_1_out_7), .in3(regbank_1_out_8),
    .out(multiplexer_2_out), .sel(register_1_q[7:6]));
  Multiplexer #(.select(2), .width(16), .enable("false")) multiplexer_3 (
    .in0(regbank_1_out_5), .in1(regbank_1_out_6), .in2(regbank_1_out_7), .in3(regbank_1_out_8),
    .out(multiplexer_3_out), .sel(register_1_q[4:3]));
  ALU alu_1 (
    .inputData1(multiplexer_2_out), .inputData2(multiplexer_3_out), .RESULT(alu_1_result),
    .ALUOP(register_1_q[11:8]));  // open: ZF
  Register #(.width(12)) register_1 (.D(ram_1_data[11:0]), .Q(register_1_q));  // open: en, clk, clr
endmodule

module regbank (
  input  LD,
  input  [1:0] REGSEL,
  input  [15:0] Din,
  input  clock,
  output [15:0] out_5,
  output [15:0] out_6,
  output [15:0] out_7,
  output [15:0] out_8
);

  wire and_1_out, and_2_out, and_3_out, and_4_out, decoder_1_out0, decoder_1_out1, decoder_1_out2,
       decoder_1_out3;

  Decoder #(.select(2)) decoder_1 (
    .out0(decoder_1_out0), .out1(decoder_1_out1), .out2(decoder_1_out2), .out3(decoder_1_out3), .sel(REGSEL));  // open: en
  and and_1 (and_1_out, decoder_1_out0, LD);
  and and_2 (and_2_out, decoder_1_out1, LD);
  and and_3 (and_3_out, decoder_1_out2, LD);
  and and_4 (and_4_out, decoder_1_out3, LD);
  Register #(.width(16)) register_1 (.D(Din), .en(and_1_out), .Q(out_5), .clk(clock));  // open: clr
  Register #(.width(16)) register_2 (.D(Din), .en(and_2_out), .Q(out_6), .clk(clock));  // open: clr
  Register #(.width(16)) register_3 (.D(Din), .en(and_3_out), .Q(out_7), .clk(clock));  // open: clr
  Register #(.width(16)) register_4 (.D(Din), .en(and_4_out), .Q(out_8), .clk(clock));  // open: clr
endmodule

module ALU (
  input  [15:0] inputData1,
  input  [15:0] inputData2,
  input  [3:0] ALUOP,
  output ZF,
  output [15:0] RESULT
);

  wire [15:0] adder_1_out, adder_2_out, and_1_out, not_1_out, or_1_out, subtractor_1_out, subtractor_2_out,
       xor_1_out;

  Adder #(.width(16)) adder_1 (.a(inputData1), .b(inputData2), .out(adder_1_out));  // open: cin, cout
  Subtractor #(.width(16)) subtractor_1 (.a(inputData1), .b(inputData2), .out(subtractor_1_out));  // open: bin, bout
  assign and_1_out = inputData1 & inputData2;  // AND_Gate and_1, 16 bits wide
  assign or_1_out = inputData1 | inputData2;  // OR_Gate or_1, 16 bits wide
  assign xor_1_out = inputData1 ^ inputData2;  // XOR_Gate xor_1, 16 bits wide
  assign not_1_out = ~inputData1;  // NOT_Gate not_1, 16 bits wide
  Adder #(.width(16)) adder_2 (.a(inputData1), .b(16'h1), .out(adder_2_out));  // open: cin, cout
  Subtractor #(.width(16)) subtractor_2 (.a(inputData1), .b(16'h1), .out(subtractor_2_out));  // open: bin, bout
  Multiplexer #(.select(4), .width(16), .enable("false")) multiplexer_1 (
    .in0(adder_1_out), .in1(subtractor_1_out), .in2(and_1_out), .in3(or_1_out), .in4(xor_1_out),
    .in5(not_1_out), .in6(inputData1), .in7(adder_2_out), .in8(subtractor_2_out), .out(RESULT), .sel(ALUOP));  // open: in9, in10, in11, in12, in13, in14, in15
  nor nor_1 (ZF, RESULT[0], RESULT[1], RESULT[2], RESULT[3], RESULT[4], RESULT[5], RESULT[6], RESULT[7], RESULT[8], RESULT[9], RESULT[10], RESULT[11], RESULT[12], RESULT[13], RESULT[14], RESULT[15]);
endmodule

module PC (
  input  PC_INC,
  output [15:0] pc
);

  wire [15:0] adder_1_out, multiplexer_1_out;

  Multiplexer #(.width(16), .enable("false")) multiplexer_1 (
    .in0(pc), .in1(adder_1_out), .out(multiplexer_1_out), .sel(PC_INC));
  Register #(.width(16)) u_PC (.D(multiplexer_1_out), .Q(pc));  // open: en, clk, clr
  Adder #(.width(16)) adder_1 (.a(pc), .b(16'h1), .out(adder_1_out));  // open: cin, cout
endmodule
